# Fritzing sketch qrng-schema (saved by Fritzing 1.0.4)
breadboards: 1

parts:
  Part1 = Arduino Uno (Rev3)
  R1 = PHOTOCELL [package=photocell]
  Mod1 = KY-008 Laser Transmitter Module [package="Breakout board"]
  R2 = PHOTOCELL [package=photocell]

nets:
  N1: Part1.A0, R1.P$1
  N2: Part1.A1, R2.P$2
  N3: Part1.D4, Part1.GND, R1.P$2, Mod1.S, Mod1.NC, Mod1.-, R2.P$1

notes:
  50/50
  Beam Splitter

custom parts:
  KY-008 Laser Transmitter Module: KY-008 Laser Transmitter Module, emits a dot shaped red laser beam.

// code stored in the sketch: Sketch.ino
int trigger = 4;
int qLeft = A0;
int qBottom = A1;

int St0 = 0;
int St1 = 0;

void setup(){
	pinMode(trigger, OUTPUT);
	Serial.begin(9600);
}

int Random(){
	// Generate pulse
	digitalWrite(trigger, HIGH);
	delay(300);
	digitalWrite(trigger, LOW);

	//read pulse
	St0 = analogRead(qLeft);
	St1 = analogRead(qBottom);

	// more "photons" on left sensor
	if(St0 > St1){
		return 0;
	} if(St0 < St1) { //more "photons" on bottom sensor
		return 1;
	}else{ // par
		Random();
	}

	delay(300);
}

void loop() {
	Serial.println(Random());
}
